# Fritzing sketch UltimaRatio (saved by Fritzing 0.9.2b)
circuit board: 4.00471cm x 10.5cm
circuit board: 4cm x 8.1cm
breadboards: 1

parts:
  IC2 = IC, DIP package, 14 pins [chip_label=MCP4922]
  XTAL2 = Crystal [frequency="16 Mhz" package=THT]
  C4 = Ceramic Capacitor [capacitance=15pF voltage=0.1kV package="100 mil [THT, multilayer]"]
  R13 = Resistor [tolerance=±5% resistance=1k package=THT]
  LED3 = LED - 3mm [color="White (4500K)" package="3 mm [THT]"]
  LED2 = LED - 3mm [color="White (4500K)" package="3 mm [THT]"]
  LED1 = LED - 3mm [color="Green (570nm)" package="3 mm [THT]"]
  R1 = Resistor [tolerance=±5% resistance=220 package=THT]
  R4 = Resistor [tolerance=±5% resistance=220 package=THT]
  R3 = Resistor [tolerance=±5% resistance=220 package=THT]
  R2 = Resistor [tolerance=±5% resistance=220 package=THT]
  U4 = Voltage Regulator - 5V [package="TO220 [THT]"]
  C1 = Electrolytic Capacitor [capacitance=3.3µF package="100 mil [THT, electrolytic]"]
  C2 = Electrolytic Capacitor [capacitance=33µF voltage=16V package="100 mil [THT, electrolytic]"]
  D1 = Rectifier Diode [part_number=1N4001 package="300 mil [THT]"]
  R16 = Resistor [tolerance=±5% resistance=10k package=THT]
  IC1 = atmega328 [part_number=ATMEGA328P-PU package=dip]
  R5 = Resistor [tolerance=±5% resistance=220 package=THT]
  R6 = Resistor [tolerance=±5% resistance=220 package=THT]
  R10 = Resistor [tolerance=±5% resistance=220 package=THT]
  R11 = Resistor [tolerance=±5% resistance=220 package=THT]
  R12 = Resistor [tolerance=±5% resistance=220 package=THT]
  R9 = Resistor [tolerance=±5% resistance=220 package=THT]
  R8 = Resistor [tolerance=±5% resistance=220 package=THT]
  R7 = Resistor [tolerance=±5% resistance=220 package=THT]
  R15 = Resistor [tolerance=±5% resistance=10k package=THT]
  R17 = Resistor [tolerance=±5% resistance=10k package=THT]
  J27 = female pin header, 1 pin [form="♀ (female)"]
  J58 = female pin header, 1 pin [form="♀ (female)"]  # not connected
  R18 = Resistor [tolerance=±5% resistance=1M package=THT]
  R14 = Resistor [tolerance=±5% resistance=4.7k package=THT]
  J59 = female pin header, 1 pin [form="♀ (female)"]
  J60 = female pin header, 1 pin [form="♀ (female)"]  # not connected
  J18 = female pin header, 1 pin [form="♀ (female)"]
  J21 = female pin header, 1 pin [form="♀ (female)"]
  J19 = female pin header, 1 pin [form="♀ (female)"]
  J20 = female pin header, 1 pin [form="♀ (female)"]
  J22 = female pin header, 1 pin [form="♀ (female)"]  # not connected
  J14 = female pin header, 1 pin [form="♀ (female)"]
  J26 = female pin header, 1 pin [form="♀ (female)"]  # not connected
  J28 = female pin header, 1 pin [form="♀ (female)"]  # not connected
  J16 = female pin header, 1 pin [form="♀ (female)"]
  J23 = female pin header, 1 pin [form="♀ (female)"]  # not connected
  J25 = female pin header, 1 pin [form="♀ (female)"]
  J61 = female pin header, 1 pin [form="♀ (female)"]
  Q1 = NPN-Transistor [package="TO92 [THT]"]
  J42 = female pin header, 1 pin [form="♀ (female)"]  # not connected
  J41 = female pin header, 1 pin [form="♀ (female)"]  # not connected
  J40 = female pin header, 1 pin [form="♀ (female)"]
  J39 = female pin header, 1 pin [form="♀ (female)"]
  J38 = female pin header, 1 pin [form="♀ (female)"]  # not connected
  J48 = female pin header, 1 pin [form="♀ (female)"]  # not connected
  J49 = female pin header, 1 pin [form="♀ (female)"]  # not connected
  J50 = female pin header, 1 pin [form="♀ (female)"]
  J51 = female pin header, 1 pin [form="♀ (female)"]
  J52 = female pin header, 1 pin [form="♀ (female)"]  # not connected
  J46 = female pin header, 1 pin [form="♀ (female)"]  # not connected
  J47 = female pin header, 1 pin [form="♀ (female)"]  # not connected
  J45 = female pin header, 1 pin [form="♀ (female)"]  # not connected
  J44 = female pin header, 1 pin [form="♀ (female)"]
  J43 = female pin header, 1 pin [form="♀ (female)"]
  J57 = female pin header, 1 pin [form="♀ (female)"]  # not connected
  J56 = female pin header, 1 pin [form="♀ (female)"]  # not connected
  J53 = female pin header, 1 pin [form="♀ (female)"]  # not connected
  J54 = female pin header, 1 pin [form="♀ (female)"]
  J55 = female pin header, 1 pin [form="♀ (female)"]
  J10 = female pin header, 1 pin [form="♀ (female)"]
  J9 = female pin header, 1 pin [form="♀ (female)"]
  J11 = female pin header, 1 pin [form="♀ (female)"]  # not connected
  J30 = male pin header, 8 pins [form="♂ (male)"]
  Upper_Connection_Bus3 = male pin header, 4 pins [form="♂ (male)"]
  lower_Connection_Bus = male pin header, 10 pins [form="♂ (male)"]
  J62 = female pin header, 1 pin [form="♀ (female)"]  # not connected
  J63 = female pin header, 1 pin [form="♀ (female)"]
  J64 = female pin header, 1 pin [form="♀ (female)"]  # not connected
  J65 = female pin header, 1 pin [form="♀ (female)"]  # not connected
  J66 = female pin header, 1 pin [form="♀ (female)"]  # not connected
  J67 = female pin header, 1 pin [form="♀ (female)"]  # not connected
  J68 = female pin header, 1 pin [form="♀ (female)"]  # not connected
  J69 = female pin header, 1 pin [form="♀ (female)"]  # not connected
  C3 = Ceramic Capacitor [capacitance=15pF voltage=0.1kV package="100 mil [THT, multilayer]"]
  Upper_Connection_Bus1 = female pin header, 8 pins [form="♀ (female)"]
  lower_Connection_Bus1 = female pin header, 10 pins [form="♀ (female)"]
  Upper_Connection_Bus2 = female pin header, 4 pins [form="♀ (female)"]
  J70 = Generic shrouded header - 10 pins [form="♂ (shrouded male)" package=THT]
  Ext = male pin header, 2 pins [form="♂ (male)"]

nets:
  N1: IC2.pin1, IC2.pin9, IC2.pin11, IC2.pin13, R13.Pin_0, U4.output_voltage, C1.+, IC1.VCC, IC1.AVCC, J30.pin2
  N2: IC2.pin3, IC1.D10_(PWM)
  N3: IC2.pin4, IC1.D13
  N4: IC2.pin5, IC1.D11_(PWM)
  N5: IC2.pin10, J30.pin3
  N6: IC2.pin14, J30.pin4
  N7: XTAL2.pin_0, IC1.XLAT2, C3.1
  N8: XTAL2.pin_1, C4.1, IC1.XLAT1
  N9: R13.Pin_1, IC1.RESET
  N10: LED3.anode, lower_Connection_Bus1.pin9
  N11: LED2.anode, R8.Pin_1
  N12: LED1.anode, R7.Pin_1
  N13: R1.Pin_0, Upper_Connection_Bus2.pin1
  N14: R1.Pin_1, Q1.B
  N15: R4.Pin_0, Upper_Connection_Bus2.pin4
  N16: R4.Pin_1, J54.pin1
  N17: R3.Pin_0, Upper_Connection_Bus2.pin3
  N18: R3.Pin_1, J44.pin1
  N19: R2.Pin_0, Upper_Connection_Bus2.pin2
  N20: R2.Pin_1, J51.pin1
  N21: U4.input_voltage, C2.+, D1.cathode
  N22: D1.anode, J70.-12V
  N23: R16.Pin_0, J9.pin1, lower_Connection_Bus1.pin3
  N24: IC1.D2, J30.pin7
  N25: IC1.D3_(PWM), R9.Pin_0
  N26: IC1.D4, R10.Pin_0
  N27: IC1.D5_(PWM), R11.Pin_0
  N28: IC1.D6_(PWM), J30.pin5
  N29: IC1.D7, lower_Connection_Bus.pin6
  N30: IC1.D8, lower_Connection_Bus.pin7
  N31: IC1.D9_(PWM), R12.Pin_0
  N32: IC1.D12, lower_Connection_Bus.pin8
  N33: IC1.A0, Upper_Connection_Bus3.pin4
  N34: IC1.A1, Upper_Connection_Bus3.pin3
  N35: IC1.A2, Upper_Connection_Bus3.pin2
  N36: IC1.A3, Upper_Connection_Bus3.pin1
  N37: IC1.A4, Ext.pin2
  N38: IC1.A5, R17.Pin_0
  N39: R5.Pin_0, Upper_Connection_Bus1.pin3
  N40: R5.Pin_1, J20.pin1
  N41: R6.Pin_0, Upper_Connection_Bus1.pin4
  N42: R6.Pin_1, J19.pin1
  N43: R10.Pin_1, lower_Connection_Bus.pin4
  N44: R11.Pin_1, lower_Connection_Bus.pin5
  N45: R12.Pin_1, lower_Connection_Bus.pin9
  N46: R9.Pin_1, lower_Connection_Bus.pin2
  N47: R8.Pin_0, Upper_Connection_Bus1.pin7
  N48: R7.Pin_0, Upper_Connection_Bus1.pin5
  N49: R15.Pin_0, J61.pin1, lower_Connection_Bus1.pin5
  N50: R17.Pin_1, lower_Connection_Bus.pin3
  N51: J27.pin1, lower_Connection_Bus1.pin4
  N52: R18.Pin_0, J59.pin1, Q1.E
  N53: R14.Pin_0, Q1.C
  N54: R14.Pin_1, J39.pin1
  N55: J18.pin1, lower_Connection_Bus1.pin2
  N56: J21.pin1, lower_Connection_Bus1.pin8
  N57: J14.pin1, lower_Connection_Bus1.pin6
  N58: J16.pin1, lower_Connection_Bus1.pin7
  N59: J25.pin1, J63.pin1
  N60: J40.pin1, J50.pin1, J43.pin1, J55.pin1, J10.pin1, Upper_Connection_Bus1.pin2

notes:
  Ultima Ratio
  K. Schade | E. Arndt
  -12V
  red stripe
  v 1.2
  THRU
  RSET
  ENV1
  ENV2
  IN
  CV
  CLK1
  CLK2

custom parts:
  Generic shrouded header - 10 pins: Generic shrouded header
